# Fritzing sketch Powerplant (saved by Fritzing 0.9.2b)
circuit board: 8.46667cm x 5.64444cm
stripboards: 2

parts:
  SN74HC595_Shift_Regester = 74HC595 [package="DIP16 [THT]"]
  UILED = LED - 5mm [color="Red (633nm)" package="5 mm [THT]"]
  Graph_10_LED = LED - 5mm [color="Green (555nm)" package="5 mm [THT]"]
  Graph_9_LED = LED - 5mm [color="Green (555nm)" package="5 mm [THT]"]
  Graph_1_LED = LED - 5mm [color="Green (555nm)" package="5 mm [THT]"]
  Graph_8_LED = LED - 5mm [color="Green (555nm)" package="5 mm [THT]"]
  Graph_7_LED = LED - 5mm [color="Green (555nm)" package="5 mm [THT]"]
  Graph_6_LED = LED - 5mm [color="Green (555nm)" package="5 mm [THT]"]
  Graph_5_LED = LED - 5mm [color="Green (555nm)" package="5 mm [THT]"]
  Graph_4_LED = LED - 5mm [color="Green (555nm)" package="5 mm [THT]"]
  Graph_3_LED = LED - 5mm [color="Green (555nm)" package="5 mm [THT]"]
  Graph_2_LED = LED - 5mm [color="Green (555nm)" package="5 mm [THT]"]
  Dump_Button = Pushbutton [package=THT]
  Power_plug1 = Power plug
  Graph_8_Resistor = Resistor [tolerance=±5% resistance=1 package=THT]
  Graph_6_Resistor = Resistor [tolerance=±5% resistance=1 package=THT]
  Graph_4_Resistor = Resistor [tolerance=±5% resistance=1 package=THT]
  Graph_3_Resistor = Resistor [tolerance=±5% resistance=1 package=THT]
  UILED_Resistor = Resistor [tolerance=±5% resistance=56 package=THT]
  Graph_2_Resistor = Resistor [tolerance=±5% resistance=1 package=THT]
  Graph_1_Resistor = Resistor [tolerance=±5% resistance=1 package=THT]
  Graph_9_Resistor = Resistor [tolerance=±5% resistance=1 package=THT]
  Power_Resistor = Resistor [tolerance=±5% resistance=10k package=THT]
  Power_Button = Pushbutton [package=THT]
  Dump_Resistor = Resistor [tolerance=±5% resistance=10k package=THT]
  U1 = SD_CARD_SOCKET [package=sdcard_4uconn]
  ProMini = Arduino Pro Mini v13
  Graph_5_Resistor = Resistor [tolerance=±5% resistance=1 package=THT]
  Graph_10_Resistor = Resistor [tolerance=±5% resistance=1 package=THT]
  Graph_7_Resistor = Resistor [tolerance=±5% resistance=1 package=THT]
  J1 = female pin header, 6 pins [form="♀ (female)"]

nets:
  N1: SN74HC595_Shift_Regester.Q1, Graph_2_Resistor.Pin_1
  N2: SN74HC595_Shift_Regester.Q2, Graph_3_Resistor.Pin_1
  N3: SN74HC595_Shift_Regester.Q3, Graph_4_Resistor.Pin_1
  N4: SN74HC595_Shift_Regester.Q4, Graph_5_Resistor.Pin_1
  N5: SN74HC595_Shift_Regester.Q5, Graph_6_Resistor.Pin_1
  N6: SN74HC595_Shift_Regester.Q6, Graph_7_Resistor.Pin_1
  N7: SN74HC595_Shift_Regester.Q7, Graph_8_Resistor.Pin_1
  GND: SN74HC595_Shift_Regester.GND, SN74HC595_Shift_Regester.OE, UILED.cathode, Graph_10_LED.cathode, Graph_9_LED.cathode, Graph_1_LED.cathode, Graph_8_LED.cathode, Graph_7_LED.cathode, Graph_6_LED.cathode, Graph_5_LED.cathode, Graph_4_LED.cathode, Graph_3_LED.cathode, Graph_2_LED.cathode, Dump_Button.leg1, Power_plug1.GND, Power_Button.leg1, U1.SH, ProMini.GND, J1.pin1, J1.pin2
  VCC: SN74HC595_Shift_Regester.MR, SN74HC595_Shift_Regester.VCC, Power_Resistor.Pin_0, Dump_Resistor.Pin_0, U1.VDD, ProMini.VCC, J1.pin3
  N8: SN74HC595_Shift_Regester.SH_CP, ProMini.D7
  N9: SN74HC595_Shift_Regester.ST_CP, ProMini.D6_PWM
  N10: SN74HC595_Shift_Regester.DS, ProMini.D5_PWM
  N11: SN74HC595_Shift_Regester.Q0, Graph_1_Resistor.Pin_1
  N12: UILED.anode, UILED_Resistor.Pin_1
  N13: Graph_10_LED.anode, Graph_10_Resistor.Pin_0
  N14: Graph_9_LED.anode, Graph_9_Resistor.Pin_0
  N15: Graph_1_LED.anode, Graph_1_Resistor.Pin_0
  N16: Graph_8_LED.anode, Graph_8_Resistor.Pin_0
  N17: Graph_7_LED.anode, Graph_7_Resistor.Pin_0
  N18: Graph_6_LED.anode, Graph_6_Resistor.Pin_0
  N19: Graph_5_LED.anode, Graph_5_Resistor.Pin_0
  N20: Graph_4_LED.anode, Graph_4_Resistor.Pin_0
  N21: Graph_3_LED.anode, Graph_3_Resistor.Pin_0
  N22: Graph_2_LED.anode, Graph_2_Resistor.Pin_0
  N23: Dump_Button.leg0, Dump_Resistor.Pin_1, ProMini.A0
  N24: Power_plug1.VCC, ProMini.RAW
  N25: UILED_Resistor.Pin_0, ProMini.D8
  N26: Graph_9_Resistor.Pin_1, ProMini.D2
  N27: Power_Resistor.Pin_1, Power_Button.leg0, ProMini.A1
  N28: U1.CD_DAT3, ProMini.D4
  N29: U1.CMD, ProMini.D11_PWM/MOSI
  N30: U1.CLK, ProMini.D13/SCK
  N31: U1.DAT0, ProMini.D12/MISO
  N32: ProMini.DTR, J1.pin6
  N33: ProMini.D0/TX, J1.pin5
  N34: ProMini.D1/RX, J1.pin4
  N35: ProMini.D3_PWM, Graph_10_Resistor.Pin_1

// code stored in the sketch: Ringoes_Powerplant_Script.ino
/*
Ringoes_Powerplant_Script.ino
V2.1.0.0
©2015 Carlin Greenfield
This script primarily operates the Sparkfun Bar Graph (Product Number:COM-09938)
The Bar Graph will go up by 4 every time the "Dump" Button (Attached to A0) is Pressed
The graph will go down pne bar every 22.5 Seconds, This can be changed by changing int SingleBarValue
This script Uses a shift Regester (Pins 5-7) to operate the bottom two bars of the Graph
The top bars are operated by pins 2 and 3.
The Power button (Attached to A1) prints the time on the clock and the level of the Graph to the Serial Port
If the Dump Button is pushed and there isn't enough room ther Error LED will blink and Coal will be set to ten.
There is an Error LED on Pin 13, this tells us that we hav either 1) tried to do somthing that we cannot (like dump a car without enough Room), or there is a problem with the board. When the Error LED Blinks it will send the Error code to the Serial port
Things in grey or after a double slash (//) Describe what the code Does

The script Folder contains 7 Files
1) The script file (Script.ino) This can only be opened by the arduio IDE (Freware, avalable from arduino.cc/download)
2) The wiring information in a .fzz file format, can only be opened by fritzing (Free software avalable from ___)
4) The changelog (Changlog.txt)
5) Information on the script (README.txt)
The last two files are Used by the program.
6) COAL.TXT (Used by the program to save the value of int Clock, DO NOT EDIT THIS.)
7) CLOCK.TXT (Used by the program to save the value of int Coal, DO NOT EDIT THIS.)*/
//Next two lines Include Libraries used for the SD Card
#include <SPI.h>
#include <SD.h>
//<Declares Pins>
const int GphDataPin=5; //Declares the Data Pin for the IC that will control the Bar Graph
const int GphClockPin=7; //Declares the Clock Pin for the IC that will control the Bar Graph
const int GphLatchPin=6; //Declares the Latch Pin for the IC that will control the Bar Graph
const int GphNine=2; //The IC only has 8 Outputs, so the top two bars of the graph have their own pins - This is pin 9
const int GphTen=3; //The IC only has 8 Outputs, so the top two bars of the graph have their own pins - This is pin 10
const int PwrBttnPin=15; // This is the input for the Power Button, 15 Tells the Board to use Analog Pin 1 as a Digital Pin
const int DmpBttnPin=14; //This is the input for the Power Button, 14 Tells the Board to use Analog Pin 0 as a Digital Pin
const int UILED=8; //This is the LED that Lights up if somthing goes wrong.
const int GphNineAndTen[]={GphNine,GphTen}; //this is an array of the 2 pins not controled by the shft Regester. It allows us to use a for loop to use the top 2 LEDs
const int ChipSelect=4; //Declares Chipselect, Used by the SD Library.
//</Declares Pins>
const int SingleBarValue=((1.5*60*1000)/(4)); //Number is equivelent to (Minutes per Car*60*1000)/(Bars per Car)
int Coal; //this will be the Bars on the Graph
int Clock; //Milliseconds
byte GphData=0; //This will be the states for Graph Bars 1-8
const int Pushed=HIGH; //Declares the meaning of pushed
int DebugMode=0;//If set to one will activate debugging, Debugging mode can also be activated by pressing power button and dump button simoltaniouslty for 1 seccond
File fileVar;

void setup() 
{
  pinMode(UILED, OUTPUT); //Sets the UILED pin as an output, this is put seperate from the rest of the pin declerations so the the UI LED can be on for the whole setup.
  digitalWrite(UILED, HIGH);//Turns on the User Interface LED, this allows us to know that the program is starting.
  //<Sets Pins as inputs and Outputs>
  pinMode(GphDataPin, OUTPUT);
  pinMode(GphClockPin, OUTPUT); 
  pinMode(GphLatchPin, OUTPUT);
  pinMode(GphNine, OUTPUT);
  pinMode(GphTen, OUTPUT);
  pinMode(ChipSelect, OUTPUT);
  pinMode(PwrBttnPin, INPUT);
  pinMode(DmpBttnPin, INPUT);
  //</Sets Pins as inputs and Outputs>
  Serial.begin(9600); //Begins Serial Communication for Debugging
  //<Initilaizes SD Card>
  if (!SD.begin(ChipSelect))//if unable to load SD card
  {//Print an error Code to the serial port NOTE: I used NOT initilized as the if statement because that is what the program is checking for, it could be reversed, I didn't
    BlinkUILED();//Blink the User interface LED
    Serial.print("millis=");//Print the Quoted text to the serial port
    Serial.print(millis());//print the return of the function millis to the serial port
    Serial.println(" Error Code=SD_Init_Failed"); //Send the error code to the Serial port
  }
  else//if the SD Card can be loaded
  {//Load States NOTE: this keeps the program from trying to load the Card if there is no SD Card present
    //<Loads stae of int Coal from SD card>
    fileVar = SD.open("COAL.TXT");//Sets File fileVar to SD.open("COAL.TXT")
    if (fileVar) //If the file can be initialized
    {//Loads the variable State
      while (fileVar.available())//While there is something to read from the file
      {
        Coal=Coal+fileVar.read(); //Add the latest charecter from the file to string data
      }
    }
    else //if the file could not be opened
    {//Prints Error Code
    ErrPrint("Cant_Open_COAL.TXT");//Prints the Error code (Quoted Text) and time of Error Code printing to the serial Port and ERRORLOG.TXT
    }
    fileVar.close(); //Close the file
    Serial.print("Coal = ");//Prints the quoted text to the serial port
    Serial.println(Coal);//Prints the value of int coal to the serial port
    //</Loads stae of int Coal from SD card>
//<Loads stae of int Clock from SD card>
  //NOTE: all the serial communications are used for debugging, I used them to get the code working, and decided not to delete them , incase they are ever needed
  fileVar = SD.open("CLOCK.TXT");//Sets File fileVar to SD.open("CLOCK.TXT")
  if (fileVar) //If the file can be initialized
  {//Loads the variable State
    while (fileVar.available()>1)//While there is something to read from the file
    {//NOTE: the int variable type isnt large enought to hold the largest possible value of Clock, so the last digit is added outside of the loop.
      Serial.print("fileVar.available() = ");//Prints the quoted text to the serial port
      Serial.println(fileVar.available()); //prints how mant bits stil need to be read
      Clock=(Clock+(fileVar.read()-48)); //Add the latest charecter from the file to string data
      Serial.print("Clock = ");//Prints the quoted text to the serial port
      Serial.println(Clock);//Prints the value of int Clock to the serial port
      Clock=Clock*10;
      Serial.print("Clock = ");//Prints the quoted text to the serial port
      Serial.println(Clock);//Prints the value of int Clock to the serial port
    }      
    Serial.print("fileVar.available() = "); //Prints the quoted text to the serial port
    Serial.println(fileVar.available()); //prints how mant bits stil need to be read
    Clock=Clock+(fileVar.read()-48); //Add the latest charecter from the file to string data
    Serial.print("Clock = "); //Prints the quoted text to the serial port
    Serial.println(Clock); //Prints the value of int Clock to the serial port
    } 
    else //if the file could not be opened
    {//Prints Error Codes
      Serial.println("Error Code=Cant_Open_CLOCK.TXT"); //Send the error code to the Serial port
    }
    fileVar.close(); //Close the file
    //</Loads stae of int Clock from SD card>
    digitalWrite(UILED, LOW);//Turns off the UILED
  }
}

void loop() 
{
  if (DebugMode==1)//if in Debugging Mode
  {
    Serial.println("void Loop");// Use the serial Port to Tell debugger that ClockCount function hasbeen called.
  }
  ClockCount(); //This counts Miliseconds, and decreases Coal by 1 every 1.5 Minutes)
  if ((digitalRead(PwrBttnPin)==Pushed)&&!(digitalRead(DmpBttnPin)==Pushed))//if ((The power button is pushed) and (the dump button is NOT pushed))
  {// NOTE: The condition is fales if both buttons are pushed because that would be ment to engage debug mode.
    PowerDown(); //Saves the state of int Coal and int Clock to the SD Card
    while((digitalRead(PwrBttnPin)==Pushed)&&!(digitalRead(DmpBttnPin)==Pushed))//while ((The power button is pushed) and (the dump button is NOT pushed))
    // NOTE: The condition is fales if both buttons are pushed because that would be ment to engage debug mode.
    {//this loop wil repeated as long as the condition is true, it keeps the program from detecting the button as being pushed twice with one long button push
      ClockCount; // will delay one milisecond and correct the clock as needed
    }
  }
  if ((digitalRead(DmpBttnPin)==Pushed)&&!(digitalRead(PwrBttnPin)==Pushed))//if ((The dump button is pushed) and (the power button is NOT pushed))
  {// NOTE: The condition is fales if both buttons are pushed because that would be ment to engage debug mode.
    Dump(); //Increases int Coal by 4, eventually will play HopperDump.wav sound.
    while((digitalRead(DmpBttnPin)==Pushed)&&!(digitalRead(PwrBttnPin)==Pushed))//while ((The dump button is pushed) and (the power button is NOT pushed))
    // NOTE: The condition is fales if both buttons are pushed because that would be ment to engage debug mode.
    {//this loop wil repeated as long as the condition is true, it keeps the program from detecting the button as being pushed twice with one long button push
      ClockCount; // will delay one milisecond and correct the clock as needed
    }
  }
  if ((digitalRead(DmpBttnPin)==Pushed)&&(digitalRead(PwrBttnPin)==Pushed))//if (the power button is pushed) and (the dump button is pushed)
  {
    Debug();//This Triggers Debug Mode if Power and Dump Buttons are Pressed at the same time for 1 second
    while((digitalRead(DmpBttnPin)==Pushed)&&(digitalRead(PwrBttnPin)==Pushed))//while ((The power button is pushed) and (the dump button is  pushed))
    {//this loop wil repeated as long as the condition is true, it keeps the program from detecting the button as being pushed twice with one long button push
      ClockCount; // will delay one milisecond and correct the clock as needed
    }
  }
  GraphLevelSet();//Sets the level of the bar graph to the level of Coal
  ErrorCheck;//Checks variables to make sure they are in peramiters
}
  
void ClockCount()
{
  if (DebugMode==1)//if in Debugging Mode
  {
    Serial.println("void ClockCount");// Use the serial Port to Tell debugger that ClockCount function hasbeen called.
  }
  delay(1); //this is a 1 milisecond delay, be sure that this only occurs once in loop
  Clock--; // Decrase the clock by one, this counts miliseconds until
  if (Clock<=0)
  {//resets clock when Time has run out NOTE: there are lines in the code that will take clock below 0 THIS IS NOT AN ERROR!!!
    Clock=SingleBarValue;//Reset Clock
  } 
  if (DebugMode==1) //If in Debug Mode
  {
    //Next 2 lines print the Value of int Coal
    Serial.print("Coal Level=");
    Serial.println(Coal);
    //Next 2 lines print the Value of int Clock
    Serial.print("Clock=");
    Serial.println(Clock);
  }
}

void GraphLevelSet()
{//This sets the level of the Bar graph
  if (DebugMode==1) //If in Debug Mode
  {
    Serial.println("void GraphLevelSet"); //Tell us that function has been called via the Serial Port
  }
  int index; //Used in For Loop
  for(index=0; index<=8; index++)//set index to 0 at begining, runs while index is < or = to 8, Changes index by 1 each time
  {
    if (DebugMode==1)
    {
      Serial.print("index=");
      Serial.println(index);
    }
    if ((Coal-1)>=index)//Coal-1 is because the index and the bit Write start at 0 and Coal starts at 1
    {
      bitWrite(GphData,index,HIGH);//Change the bit in byte GphData, position "index" to HIGH
    }
    else
    {
      bitWrite(GphData,index,LOW); //Change the bit in byte GphData, position "index" to LOW
    }
  }
      if (DebugMode==1)
    {
      Serial.print("GphData=");
      Serial.println(GphData);
    }
  shiftOut(GphDataPin, GphClockPin, MSBFIRST, GphData);//Send GphData to the shift Regester.
  //the next two  lines triger the latch pin to tell the shift regester to write the data.
  digitalWrite(GphLatchPin, HIGH);
  digitalWrite(GphLatchPin, LOW);
  //<deal with the 2 pins that arnt controled by the shift regester.>
  for(index=0; index<=1; index++)//set index to 0 at begining, runs while index is < or = to 8, Changes index by 1 each time
  {
    if ((Coal-9)>=index)//Coal-9 is because the index 0 controls the 9th Line of the Graph
    {
      digitalWrite(GphNineAndTen[index],HIGH); //Send power to Pin "GphNineAndTen[index]"
    }
    else
    {
      digitalWrite(GphNineAndTen[index],LOW); //kill power to Pin "GphNineAndTen[index]"
    }
  }
}

void Dump()
{
  int Delay=250; //declare the Delay, this keeps the function from beeing called twice with a single push.
  if (DebugMode==1)//if in Debugging Mode
  {
    Serial.println("void Dump"); //Tell us that function has been called via the Serial Port
  }
  if (Coal<=6)//if there is room for the car to be dumped
  {
    Coal=Coal+4;//Change Coal by 4
    //Play Hopper_Dump.wav
  }
  else // if there isn't room for the car to be dumped
  {
    Coal=10;// Set Coal to It's Max Value
    GraphLevelSet();//Sets the Level of the Bar Graph NOTE: this makes the bar graph represent the coal Level Immidiatly, instead of after the LED Blinks
    ErrPrint("Too_Much_Coal");//Prints the Error code (Quoted Text) and time of Error Code printing to the serial Port and ERRORLOG.TXT
    //Save Error Code to Log.txt on SD Card along with time since reset
  }
  delay(Delay);//Delay so that the function isn't invoked multiple times by a single button Press. 
}

void BlinkUILED()
{//Blinks the User Interface LED
  int Delay=500;//The time btween Blinks
  digitalWrite(UILED, HIGH);//Turn On the LED
  delay(Delay);//Wait for Delay Msecs
  digitalWrite(UILED, LOW); //Turn Off LED
  delay(Delay);//Wait for Delay Msecs
  digitalWrite(UILED, HIGH);//Turn On the LED
  delay(Delay);//Wait for Delay Msecs
  digitalWrite(UILED, LOW); //Turn Off LED
  Clock=Clock-(Delay*3); //Make up for Time Lost
}

void Debug()
{//This Triggers Debug Mode if Power and Dump Buttons are Pressed at the same time for 1 second
  if (DebugMode==1)//if in Debugging Mode
  {
    Serial.println("void Debug"); //Tell us that function has been called via the Serial Port
  }
  int Delay=1000;//declare Variable Delay and set it to 1000 - NOTE the delay command uses miliseconds, so take seconds and multiply by 1000
  digitalWrite(UILED,HIGH);//Turn on the User Interface LED
  if (DebugMode==0)//if not in Debug Mode
  {
    Serial.println("Continue holding buttons to enter Debugging Mode.");//Print "Continue holding buttons to enter Debugging Mode." to the serial Port
  }
  else if (DebugMode==1)//if in Debugging Mode - NOTE; else if will only be invoked if above is false
  {
    Serial.println("Continue holding buttons to exit Debugging Mode.");//Print "Continue holding buttons to exit Debugging Mode." to the serial Port
  }
  delay(Delay);//wait for "Delay" msecs
  if ((digitalRead(DmpBttnPin)==Pushed)&&(digitalRead(PwrBttnPin)==Pushed))//if both Power and Dump Buttons are Still Pushed
  {
    if (DebugMode==0) //if not in Debug Mode
    {
      DebugMode=1;//activate Debug Mode
      Serial.println("Debugging Mode Activated");//Tell us that we have activated Debug Mode via the serial Port
    }
    else if (DebugMode==1)//if in Debugging Mode - NOTE; else if will only be invoked if above is false
    {
      DebugMode=0;//deactivate Debug Mode
      Serial.println("Debugging Mode Deactivated");//Tell us that we have deactivated Debug Mode via the serial Port
    }
  }
  if ((digitalRead(DmpBttnPin)!=Pushed)||(digitalRead(PwrBttnPin)!=Pushed))//if either Power and Dump Buttons are not Still Pushed
  {
    if (DebugMode==0) //if not in Debug Mode
    {
      Serial.println("Debugging Mode activation Cancled");//Tell us that we have not activated Debug Mode via the serial Port
    }
    else if (DebugMode==1)//if in Debugging Mode - NOTE; else if will only be invoked if above is false
    {
      Serial.println("Debugging Mode Deactivatation Cancelled");//Tell us that we have not deactivated Debug Mode via the serial Port
    }
  }  
  digitalWrite(UILED,LOW);//turn of the User interface LED
  Clock=Clock-Delay;//Corect the Clock
}

void ErrorCheck()
{
  //Checks Errors
  //NOTE: None of these should be true, this is an ERROR checker
  if (Coal<0) //if Coal < 0
  {
    Coal=0; //Set Coal to 0
    ErrPrint("Coal_<_0");//Prints the Error code (Quoted Text) and time of Error Code printing to the serial Port and ERRORLOG.TXT
  }
  if (Coal>10) //if Coal > 10
  {
    Coal=10; //Set Coal to 0
    ErrPrint("Coal_>_10");//Prints the Error code (Quoted Text) and time of Error Code printing to the serial Port and ERRORLOG.TXT
  }
  if (Clock>SingleBarValue)
  {
    Clock=SingleBarValue;//Reset Clock
    ErrPrint("Clock_>_SingleBarValue");//Prints the Error code (Quoted Text) and time of Error Code printing to the serial Port and ERRORLOG.TXT
  }
}

void ErrPrint(String ErrCode)
{ //This prints an error code to the serial port and Blinks the UILED
  digitalWrite(UILED, HIGH);
  Serial.print("Millis="); //Print the quoted text to the file
  Serial.print(millis()); //Print the value of millis to the file
  Serial.print("  Error Code="); //print the quoted text to the file
  Serial.println(ErrCode);//print the error code to the file
  if (!SD.begin(ChipSelect))//if unable to load SD card
    {//Print an error Code to the serial port NOTE: I used NOT initilized as the if statement because that is what the program is checking for, it could be reversed, I didn't
      BlinkUILED();//Blink the User interface LED
      Serial.print("millis=");//Print the Quoted text to the serial port
      Serial.print(millis());//print the return of the function millis to the serial port
      Serial.println("  Error Code=SD_Init_Failed"); //Send the error code to the Serial port
    }
  else//if the SD Card can be loaded
  {
    //Next 3 lines print the Value of int Coal
    fileVar = SD.open("ERRORLOG.TXT", FILE_WRITE);//Sets the File fileVar to a command that opens the file for writing
    if (fileVar)//if the file can be opened
    {
      fileVar.print("Millis="); //Print the quoted text to the file
      fileVar.print(millis()); //Print the value of millis to the file
      fileVar.print("  Error Code="); //print the quoted text to the file
      fileVar.println(ErrCode);//print the error code to the file
      fileVar.close();// close the file
    }
    else
    {
      // if the file didn't open, print an error:
      Serial.println("Error Code=Cant_Open_COAL.TXT_Powerdown");//Prints the quoted text to the serial port
    }
    BlinkUILED();
  }
}

void PowerDown()
{//this saves the value of int Clock and int Coal to the SD card, it also prints them to the serial port
  digitalWrite(UILED, HIGH); //Turns on the Error LED
  if (DebugMode==1) //If in Debug Mode
  {
    Serial.println("void PowerDown"); //Tell us that function has been called via the Serial Port
  }
  //Next 3 lines print the Value of int Coal
  SD.remove("COAL.TXT");//Delete the old value of int Coal from the txt file
  fileVar = SD.open("COAL.TXT", FILE_WRITE);//Sets the File fileVar to a command that opens the file for writing
  if (fileVar)//if the file can be opened
  {
    Serial.print("Writing to COAL.TXT...");//Prints the quoted text to the serial port
    fileVar.write(Coal);//Write the VALUE of coal to the text file, NOT the the ASCII charecters for it.
    fileVar.close();// close the file
    Serial.println("done.");//Prints the quoted text to the serial port
  }
  else
  {
    // if the file didn't open, print an error:
    ErrPrint("Cant_Open_COAL.TXT_Powerdown");//Prints the Error code (Quoted Text) and time of Error Code printing to the serial Port and ERRORLOG.TXT
  }
  SD.remove("CLOCK.TXT");//Delete the old value of int Clock from the txt file
  fileVar = SD.open("CLOCK.TXT", FILE_WRITE); //Sets the File fileVar to a command that opens the file for writing
  if (fileVar) //if the file can be opened
  {
    Serial.print("Writing to CLOCK.TXT...");//Prints the quoted text to the serial port
    fileVar.print(Clock); //Write the ASCII NUMBERS that MAKE UP the value of the variable to the file
    fileVar.close();// close the file
    Serial.println("done.");//Prints the quoted text to the serial port
  }
  else //If the file couldnt be opened
  {
    Serial.println("Error Code=Cant_Open_CLOCK.TXT_Powerdown");//Prints the quoted text to the serial port
  }
  
  Serial.println("Power Down Complete");//Prints the quoted text to the serial port
  Serial.print("int Coal = ");//Prints the quoted text to the serial port
  Serial.println(Coal);//Prints the value of int Clock to the serial port
  Serial.print("int Clock = ");//Prints the quoted text to the serial port
  Serial.println(Clock);//Prints the value of int Clock to the serial port
  BlinkUILED(); //Blink the User interface LED
}
